# Fritzing sketch dynamo_power_v1 (saved by Fritzing 0.9.10b)
breadboards: 1

parts:
  U1 = Voltage Regulator - 5V [package="TO220 [THT]"]
  D1 = bridge rectifier round [package="round [THT]"]
  R1 = Resistor [tolerance=±5% resistance=47k mn=51K package="1206 [SMD]"]
  R2 = Resistor [tolerance=±5% resistance=220 mn=51K package="1206 [SMD]"]
  R3 = Resistor [tolerance=±5% resistance=220 mn=43K package="1206 [SMD]"]
  R4 = Resistor [tolerance=±5% resistance=220 mn=75K package="1206 [SMD]"]
  C3 = Tantalum Capacitor [capacitance=22µF voltage=35V package="100 mil [THT, tantalum]"]
  C2 = Tantalum Capacitor [capacitance=1.47mF voltage=35V mn=0.47uF package="100 mil [THT, tantalum]"]
  C1 = Capacitor Polarized [mn=22uF package=panasonic_d]
  D2 = SOLAR-IXYS [package=solarbit-12x1]

nets:
  N1: U1.input_voltage, R3.Pin_1, R4.Pin_1, C2.+
  N2: U1.GND, D1.DC-, R1.Pin_0, R2.Pin_0, C3.-, C2.-, C1.-
  N3: U1.output_voltage, D1.DC+, C3.+, C1.+
  N4: D1.AC#0, D2.C
  N5: D1.AC#1, D2.A
  N6: R1.Pin_1, R3.Pin_0
  N7: R2.Pin_1, R4.Pin_0
