# Fritzing sketch dynamo_v2_noresistors (saved by Fritzing 0.9.10b)
breadboards: 1

parts:
  D1 = bridge rectifier round [package="round [THT]"]
  C3 = Tantalum Capacitor [capacitance=22µF voltage=35V package="100 mil [THT, tantalum]"]
  C2 = Tantalum Capacitor [capacitance=1.47mF voltage=35V mn=0.47uF package="100 mil [THT, tantalum]"]
  C1 = Capacitor Polarized [mn=2200uF package=panasonic_d]
  D2 = SOLAR-IXYS [package=solarbit-12x1]
  U1 = Voltage Regulator - 5V [package="TO220 [THT]"]

nets:
  N1: D1.AC#0, D2.C
  N2: D1.AC#1, D2.A
  N3: D1.DC+, C3.+, C1.+, U1.input_voltage
  N4: D1.DC-, C3.-, C2.-, C1.-, U1.GND
  N5: C2.+, U1.output_voltage

notes:
  out -
  out +
  dynamo
  bridge rectifier
  tantalum
  electrolytic
  load +
  load -
