# Fritzing sketch attiny_DFplayer (saved by Fritzing 0.9.10b)
breadboards: 1

parts:
  U1 = attiny85 [package=dip]
  DFRobot_DFPlayer_Mini1 = DFRobot DFPlayer Mini [part_number=DFR0299]
  SP1 = SPEAKER [package=pcb_mount_speaker]
  D1 = SOLAR-IXYS [mn=5V package=solarbit-12x1]
  R1 = Resistor [tolerance=±5% power=0.25 resistance=1k package=THT]

nets:
  N1: U1.Pin_4, DFRobot_DFPlayer_Mini1.GND-1, DFRobot_DFPlayer_Mini1.GND-2, D1.C
  N2: U1.Pin_6, DFRobot_DFPlayer_Mini1.TX
  N3: U1.Pin_7, R1.Pin_1
  N4: U1.Pin_8, DFRobot_DFPlayer_Mini1.VCC, D1.A
  N5: DFRobot_DFPlayer_Mini1.RX, R1.Pin_0
  N6: DFRobot_DFPlayer_Mini1.SPK_1, SP1.-
  N7: DFRobot_DFPlayer_Mini1.SPK_2, SP1.+
