# Fritzing sketch hex_schmitt_inverter (saved by Fritzing 0.9.10b)
breadboards: 1

parts:
  BAT1 = BC9VPC [mn=9V package=bc9vpc]
  U1 = SN74LS14N [mn=CD40106 mpn="HEX SCHMITT CONVERTER" package="DIP14 [THT]"]
  C1 = Capacitor [mn=0.1uF package=cap-pth-small2]
  R1 = Resistor [tolerance=±5% resistance=10k package="1206 [SMD]"]
  J1 = Basic Force Sensing Resistor (FSR) [mn="variable res" package=THT]
  J2 = Basic Force Sensing Resistor (FSR) [mn="variable res" package=THT]
  J3 = Basic Force Sensing Resistor (FSR) [mn="variable res" package=THT]
  J4 = Basic Force Sensing Resistor (FSR) [mn="variable res" package=THT]
  J5 = Basic Force Sensing Resistor (FSR) [mn="variable res" package=THT]
  J6 = Basic Force Sensing Resistor (FSR) [mn="variable res" package=THT]
  C2 = Capacitor [mn=0.1uF package=cap-pth-small2]
  C3 = Capacitor [mn=0.1uF package=cap-pth-small2]
  C4 = Capacitor [mn=0.1uF package=cap-pth-small2]
  C5 = Capacitor [mn=0.1uF package=cap-pth-small2]
  C6 = Capacitor [mn=0.1uF package=cap-pth-small2]
  R2 = Resistor [tolerance=±5% resistance=10k package="1206 [SMD]"]
  R3 = Resistor [tolerance=±5% resistance=10k package="1206 [SMD]"]
  R4 = Resistor [tolerance=±5% resistance=10k package="1206 [SMD]"]
  R5 = Resistor [tolerance=±5% resistance=10k package="1206 [SMD]"]
  R6 = Resistor [tolerance=±5% resistance=10k package="1206 [SMD]"]
  S1 = Toggle Switch [package=THT]

nets (from the schematic view):
  N1: BAT1.V+, S1.COM
  N2: BAT1.V-, U1.GND, C1.1, C2.1, C3.1, C4.2, C5.2, C6.2
  N3: U1.1A, C1.2, J4.pin_1
  N4: U1.1Y, J4.pin_0, R4.Pin_0
  N5: U1.2A, J5.pin_1, C2.2
  N6: U1.2Y, J5.pin_0, R5.Pin_0
  N7: U1.3A, J6.pin_1, C3.2
  N8: U1.3Y, J6.pin_0, R6.Pin_0
  N9: U1.4Y, J3.pin_1, R2.Pin_1
  N10: U1.4A, J3.pin_0, C6.1
  N11: U1.5Y, R1.Pin_1, J2.pin_1
  N12: U1.5A, J2.pin_0, C5.1
  N13: U1.6Y, J1.pin_1, R3.Pin_1
  N14: U1.6A, J1.pin_0, C4.1
  N15: U1.VCC, R1.Pin_0, R2.Pin_0, R3.Pin_0, R4.Pin_1, R5.Pin_1, R6.Pin_1, S1.L2
